# Fritzing sketch circuit_idea_lab5 (saved by Fritzing 0.9.3b)
breadboards: 1

parts:
  Part1 = Adafruit Metro Mini [part_number="Adafruit #2590"]
  VCC1 = Battery block 9V
  SERVO1 = Adafruit Feedback Servo (small)
  SW1 = ToggleSW_Blue1

nets:
  N1: Part1.IO10, SERVO1.Signal
  N2: Part1.IO2, SW1.Pin0
  N3: Part1.+5V, SERVO1.Power, SW1.pin_1
  N4: Part1.GND, VCC1.-, SERVO1.Ground, SW1.pin_2
  N5: Part1.VIN, VCC1.+

custom parts:
  Adafruit Metro Mini: We sure love the ATmega328 here at Adafruit, and we use them a lot for our own projects. The processor has plenty of GPIO, Analog inputs, hardware UART SPI and I2C, timers and PWM galore - just enough for most simple projects. When we need to go small, we use a Pro Trinket 3V or 5V, but if you want to have USB-to-Serial built in, we reach for an Adafruit METRO Mini. METRO Mini is the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
  Adafruit Feedback Servo (small): Adafruit Feedback Servo (Small)
  ToggleSW_Blue1: Generic Tiggle Switch on-off-on
